# Fritzing sketch automatedFan (saved by Fritzing 0.9.3b)
breadboards: 2

parts:
  S1 = Pushbutton [package="[THT]"]
  S2 = Pushbutton [package="[THT]"]
  S3 = Pushbutton [package="[THT]"]
  hc-sr1 = hc-sr04
  M1 = DC Motor
  VCC1 = Battery block 9V
  Part1 = Thumb Joystick
  Part2 = Arduino Uno (Rev3) - ICSP
  LCD1 = LCD screen
  J1 = Basic Servo
  R1 = Resistor [tolerance=±5% resistance=330 package=THT]
  R2 = Resistor [tolerance=±5% resistance=10 package="0402 [SMD]"]
  R3 = Resistor [tolerance=±5% resistance=330 package="1206 [SMD]"]
  R4 = Resistor [tolerance=±5% resistance=10k package="0402 [SMD]"]
  R6 = Resistor [tolerance=±5% resistance=10k package="0402 [SMD]"]
  R7 = Resistor [tolerance=±5% resistance=10k package="0402 [SMD]"]
  Q1 = NPN-Transistor [package="SOT-23 [SMD]"]
  D1 = Rectifier Diode [part_number=1N4001 package="300 mil [THT]"]

nets:
  VCC: S1.Pin_1, S1.Pin_2, S2.Pin_1, S2.Pin_2, S3.Pin_1, S3.Pin_2, hc-sr1.VCC, hc-sr1.Trig, Part1.VCC, Part2.A0, Part2.5V, LCD1.VDD, J1.vcc
  N1: S1.Pin_3, S1.Pin_4, Part2.D8, R7.Pin_0
  N2: S2.Pin_3, S2.Pin_4, Part2.D7, R6.Pin_0
  N3: S3.Pin_3, S3.Pin_4, Part2.D10_PWM/SS, R4.Pin_0
  N4: hc-sr1.Echo, Part2.A1
  GND: hc-sr1.GND, VCC1.-, Part1.GND, Part2.GND, LCD1.VSS, LCD1.R/W, LCD1.LED-, R1.Pin_0, R2.Pin_1, R4.Pin_1, R6.Pin_1, R7.Pin_1, Q1.2
  N5: M1.pin_1, VCC1.+, D1.cathode
  N6: M1.pin_2, Q1.1, D1.anode
  N7: Part1.SEL, Part2.D13/SCK
  N8: Part1.HORZ, Part2.A3
  N9: Part1.VERT, Part2.A4/SDA
  N10: Part2.ICSP_MOSI, Part2.D11_PWM/MOSI, LCD1.E
  N11: Part2.D12/MISO, LCD1.RS
  N12: Part2.D2, LCD1.DB7
  N13: Part2.D3_PWM, R3.Pin_0
  N14: Part2.D4, LCD1.DB6
  N15: Part2.D5_PWM, LCD1.DB5
  N16: Part2.D6_PWM, LCD1.DB4
  N17: LCD1.V0, R1.Pin_1
  N18: LCD1.LED+, R2.Pin_0
  N19: R3.Pin_1, Q1.0

notes:
  GY-521,
  VCC
  GND
  SCL
  SDA
